// Logisim project logisimlib.circ as structural Verilog
// 2x1 MUX
module mux_2x1_1b (
  input  I0,
  input  I1,
  input  Op,
  output O
);

  wire and_1_out, and_2_out;

  and and_1 (and_1_out, I0, ~Op);  // AND_Gate
  and and_2 (and_2_out, I1, Op);
  or or_1 (O, and_1_out, and_2_out);
endmodule

// 2x1 MUX
module mux_2x1_4b (
  input  [3:0] I0,
  input  Op,
  input  [3:0] I1,
  output [3:0] O
);

  mux_2x1_1b mux_2x1_1b_1 (.O(O[0]), .I1(I1[0]), .I0(I0[0]), .Op(Op));
  mux_2x1_1b mux_2x1_1b_2 (.O(O[1]), .I1(I1[1]), .I0(I0[1]), .Op(Op));
  mux_2x1_1b mux_2x1_1b_3 (.O(O[2]), .I1(I1[2]), .I0(I0[2]), .Op(Op));
  mux_2x1_1b mux_2x1_1b_4 (.O(O[3]), .I1(I1[3]), .I0(I0[3]), .Op(Op));
endmodule

// 2x1 MUX
module mux_2x1_16b (
  input  [15:0] I0,
  input  Op,
  input  [15:0] I1,
  output [15:0] O
);

  mux_2x1_4b mux_2x1_4b_1 (.O(O[3:0]), .I0(I0[3:0]), .I1(I1[3:0]), .Op(Op));
  mux_2x1_4b mux_2x1_4b_2 (.O(O[7:4]), .I0(I0[7:4]), .I1(I1[7:4]), .Op(Op));
  mux_2x1_4b mux_2x1_4b_3 (.O(O[11:8]), .I0(I0[11:8]), .I1(I1[11:8]), .Op(Op));
  mux_2x1_4b mux_2x1_4b_4 (.O(O[15:12]), .I0(I0[15:12]), .I1(I1[15:12]), .Op(Op));
endmodule

// 4x1 MUX
module mux_4x1_1b (
  input  I0,
  input  I1,
  input  I2,
  input  I3,
  input  [1:0] Op,
  output O
);

  wire mux_2x1_1b_1_o, mux_2x1_1b_2_o;

  mux_2x1_1b mux_2x1_1b_1 (.O(mux_2x1_1b_1_o), .I1(I1), .I0(I0), .Op(Op[0]));
  mux_2x1_1b mux_2x1_1b_2 (.O(mux_2x1_1b_2_o), .I1(I3), .I0(I2), .Op(Op[0]));
  mux_2x1_1b mux_2x1_1b_3 (.O(O), .I1(mux_2x1_1b_2_o), .I0(mux_2x1_1b_1_o), .Op(Op[1]));
endmodule

// 4x1 MUX
module mux_4x1_16b (
  input  [15:0] I0,
  input  [15:0] I1,
  input  [15:0] I2,
  input  [15:0] I3,
  input  [1:0] Op,
  output [15:0] O
);

  wire [15:0] mux_2x1_16b_1_o, mux_2x1_16b_2_o;

  mux_2x1_16b mux_2x1_16b_1 (.O(mux_2x1_16b_1_o), .I0(I0), .I1(I1), .Op(Op[0]));
  mux_2x1_16b mux_2x1_16b_2 (.O(mux_2x1_16b_2_o), .I0(I2), .I1(I3), .Op(Op[0]));
  mux_2x1_16b mux_2x1_16b_3 (.O(O), .I0(mux_2x1_16b_1_o), .I1(mux_2x1_16b_2_o), .Op(Op[1]));
endmodule

// 2x4 DEC
module dec_2x4_1b (
  input  [1:0] i,
  output O0,
  output O1,
  output O2,
  output O3
);

  and and_1 (O0, ~i[0], ~i[1]);  // AND_Gate
  and and_2 (O1, i[0], ~i[1]);  // AND_Gate
  and and_3 (O2, ~i[0], i[1]);  // AND_Gate
  and and_4 (O3, i[0], i[1]);
endmodule

// D LATCH
module d_latch (
  input  d,
  input  Clk,
  input  Clr,
  output Q,
  output QP
);

  wire a1_out, na1_out, na2_out;

  nand na2 (na2_out, Clk, ~d);  // NAND_Gate
  nand na1 (na1_out, d, Clk);
  and a1 (a1_out, na2_out, ~Clr);  // AND_Gate
  nand na3 (Q, na1_out, QP);
  nand na4 (QP, Q, a1_out);
endmodule

// D FLIP
module d_flip_flop (
  input  d,
  input  Clr,
  input  Clk,
  output Q,
  output QP
);

  wire dl1_q, dl1_qp, not_1_out;

  d_latch dl1 (.QP(dl1_qp), .Q(dl1_q), .Clk(Clk), .Clr(Clr), .d(d));
  // NoConnect on dl1_qp
  not not_1 (not_1_out, Clk);
  d_latch dl2 (.QP(QP), .Q(Q), .Clk(not_1_out), .Clr(Clr), .d(dl1_q));
endmodule

// HALF ADDER
module half_adder (
  input  x,
  input  y,
  output S,
  output C
);

  wire nand_1_out, nand_2_out;

  nand nand_1 (nand_1_out, x, ~y);  // NAND_Gate
  nand nand_2 (nand_2_out, ~x, y);  // NAND_Gate
  nand nand_3 (S, nand_1_out, nand_2_out);
  and and_1 (C, x, y);
endmodule

// FULL ADDER
module full_adder (
  input  x,
  input  y,
  input  Cin,
  output S,
  output COUT
);

  wire half_adder_1_c, half_adder_1_s, half_adder_2_c;

  half_adder half_adder_1 (.C(half_adder_1_c), .S(half_adder_1_s), .y(y), .x(x));
  half_adder half_adder_2 (.C(half_adder_2_c), .S(S), .y(Cin), .x(half_adder_1_s));
  or or_1 (COUT, half_adder_2_c, half_adder_1_c);
endmodule

// REG 4B
module reg_4b (
  input  Clr,
  input  Clk,
  input  [3:0] d,
  output [3:0] Q
);

  wire d_flip_flop_1_qp, d_flip_flop_2_qp, d_flip_flop_3_qp, d_flip_flop_4_qp;

  d_flip_flop d_flip_flop_1 (.QP(d_flip_flop_1_qp), .Q(Q[0]), .Clr(Clr), .Clk(Clk), .d(d[0]));
  d_flip_flop d_flip_flop_2 (.QP(d_flip_flop_2_qp), .Q(Q[1]), .Clr(Clr), .Clk(Clk), .d(d[1]));
  d_flip_flop d_flip_flop_3 (.QP(d_flip_flop_3_qp), .Q(Q[2]), .Clr(Clr), .Clk(Clk), .d(d[2]));
  d_flip_flop d_flip_flop_4 (.QP(d_flip_flop_4_qp), .Q(Q[3]), .Clr(Clr), .Clk(Clk), .d(d[3]));
  // NoConnect on d_flip_flop_1_qp
  // NoConnect on d_flip_flop_2_qp
  // NoConnect on d_flip_flop_3_qp
  // NoConnect on d_flip_flop_4_qp
endmodule

// REG 16B
module reg_16b (
  input  Clr,
  input  Clk,
  input  [15:0] d,
  output [15:0] Q
);

  reg_4b reg_4b_1 (.Q(Q[3:0]), .d(d[3:0]), .Clr(Clr), .Clk(Clk));
  reg_4b reg_4b_2 (.Q(Q[7:4]), .d(d[7:4]), .Clr(Clr), .Clk(Clk));
  reg_4b reg_4b_3 (.Q(Q[11:8]), .d(d[11:8]), .Clr(Clr), .Clk(Clk));
  reg_4b reg_4b_4 (.Q(Q[15:12]), .d(d[15:12]), .Clr(Clr), .Clk(Clk));
endmodule

// REGFILE 4X 16B
module regfile_4x_16b (
  input  [1:0] Rreg1,
  input  Clk,
  input  Ewreg,
  input  [1:0] Rreg2,
  input  [1:0] Wreg,
  input  [15:0] d,
  output [15:0] REG1,
  output [15:0] REG2
);

  wire and_1_out, and_2_out, and_3_out, dec_2x4_1b_1_o0, dec_2x4_1b_1_o1, dec_2x4_1b_1_o2, dec_2x4_1b_1_o3,
       undriven_2;
  wire [15:0] reg_16b_1_q, reg_16b_2_q, reg_16b_3_q, undriven, zero_reg_q;

  dec_2x4_1b dec_2x4_1b_1 (
    .O1(dec_2x4_1b_1_o1), .O2(dec_2x4_1b_1_o2), .O3(dec_2x4_1b_1_o3), .O0(dec_2x4_1b_1_o0), .i(Wreg));
  // NoConnect on dec_2x4_1b_1_o0
  and and_1 (and_1_out, Ewreg, dec_2x4_1b_1_o1, Clk);
  and and_2 (and_2_out, Ewreg, dec_2x4_1b_1_o2, Clk);
  and and_3 (and_3_out, Ewreg, dec_2x4_1b_1_o3, Clk);
  reg_16b zero_reg (.Q(zero_reg_q), .Clk(undriven_2), .Clr(1'b1), .d(undriven));
  // NoConnect on undriven
  // NoConnect on undriven_2
  reg_16b reg_16b_1 (.Q(reg_16b_1_q), .Clk(and_1_out), .Clr(1'b0), .d(d));
  reg_16b reg_16b_2 (.Q(reg_16b_2_q), .Clk(and_2_out), .Clr(1'b0), .d(d));
  reg_16b reg_16b_3 (.Q(reg_16b_3_q), .Clk(and_3_out), .Clr(1'b0), .d(d));
  mux_4x1_16b mux_4x1_16b_1 (
    .O(REG1), .I1(reg_16b_1_q), .I2(reg_16b_2_q), .I3(reg_16b_3_q), .I0(zero_reg_q), .Op(Rreg1));
  mux_4x1_16b mux_4x1_16b_2 (
    .O(REG2), .I1(reg_16b_1_q), .I2(reg_16b_2_q), .I3(reg_16b_3_q), .I0(zero_reg_q), .Op(Rreg2));
endmodule

// ALU 1B
module alu_1b (
  input  [2:0] Op,
  input  x,
  input  y,
  input  Less,
  input  Cin,
  output R,
  output SET,
  output COUT,
  output O
);

  wire and_1_out, full_adder_1_cout, or_1_out, xor_1_out, xor_2_out;

  xor xor_1 (xor_1_out, y, Op[2]);
  full_adder full_adder_1 (.S(SET), .COUT(full_adder_1_cout), .y(xor_1_out), .Cin(Cin), .x(x));
  and and_1 (and_1_out, x, xor_1_out);
  or or_1 (or_1_out, x, xor_1_out);
  xor xor_2 (xor_2_out, Cin, full_adder_1_cout);
  mux_4x1_1b mux_4x1_1b_1 (.O(R), .I0(and_1_out), .I1(or_1_out), .I2(SET), .I3(Less), .Op(Op[1:0]));
  and and_2 (COUT, Op[1], full_adder_1_cout);
  and and_3 (O, Op[1], xor_2_out);
endmodule

// ALU 4B O
module alu_4b_open (
  input  [3:0] x,
  input  [2:0] Op,
  input  Less,
  input  Cin,
  input  [3:0] y,
  output [3:0] R,
  output ZERO,
  output O,
  output SET,
  output COUT
);

  wire alu_1b_1_cout, alu_1b_1_o, alu_1b_1_set, alu_1b_2_cout, alu_1b_2_o, alu_1b_2_set, alu_1b_3_cout,
       alu_1b_3_o, alu_1b_3_set;

  alu_1b alu_1b_1 (
    .R(R[0]), .SET(alu_1b_1_set), .COUT(alu_1b_1_cout), .O(alu_1b_1_o), .Op(Op), .y(y[0]), .Less(Less),
    .Cin(Cin), .x(x[0]));
  alu_1b alu_1b_2 (
    .R(R[1]), .SET(alu_1b_2_set), .COUT(alu_1b_2_cout), .O(alu_1b_2_o), .Op(Op), .y(y[1]), .Less(1'b0),
    .Cin(alu_1b_1_cout), .x(x[1]));
  alu_1b alu_1b_3 (
    .R(R[2]), .SET(alu_1b_3_set), .COUT(alu_1b_3_cout), .O(alu_1b_3_o), .Op(Op), .y(y[2]), .Less(1'b0),
    .Cin(alu_1b_2_cout), .x(x[2]));
  alu_1b alu_1b_4 (
    .R(R[3]), .SET(SET), .COUT(COUT), .O(O), .Op(Op), .y(y[3]), .Less(1'b0), .Cin(alu_1b_3_cout), .x(x[3]));
  // NoConnect on alu_1b_1_o
  // NoConnect on alu_1b_1_set
  // NoConnect on alu_1b_2_o
  // NoConnect on alu_1b_2_set
  // NoConnect on alu_1b_3_o
  // NoConnect on alu_1b_3_set
  and and_1 (ZERO, ~R[0], ~R[1], ~R[2], ~R[3]);  // AND_Gate
endmodule

// ALU 4B
module alu_4b (
  input  [2:0] Op,
  input  [3:0] x,
  input  [3:0] y,
  output [3:0] R,
  output O,
  output ZERO
);

  wire alu_4b_open_1_cout, alu_4b_open_1_set;

  alu_4b_open alu_4b_open_1 (
    .O(O), .SET(alu_4b_open_1_set), .COUT(alu_4b_open_1_cout), .R(R), .ZERO(ZERO), .Less(alu_4b_open_1_set),
    .Cin(Op[2]), .x(x), .y(y), .Op(Op));
  // NoConnect on alu_4b_open_1_cout
endmodule

// ALU 16B O
module alu_16b_open (
  input  [15:0] x,
  input  [2:0] Op,
  input  Less,
  input  Cin,
  input  [15:0] y,
  output [15:0] R,
  output ZERO,
  output O,
  output SET,
  output COUT
);

  wire alu_4b_open_1_cout, alu_4b_open_1_o, alu_4b_open_1_set, alu_4b_open_1_zero, alu_4b_open_2_cout,
       alu_4b_open_2_o, alu_4b_open_2_set, alu_4b_open_2_zero, alu_4b_open_3_cout, alu_4b_open_3_o,
       alu_4b_open_3_set, alu_4b_open_3_zero, alu_4b_open_4_zero;

  alu_4b_open alu_4b_open_1 (
    .O(alu_4b_open_1_o), .SET(alu_4b_open_1_set), .COUT(alu_4b_open_1_cout), .R(R[3:0]),
    .ZERO(alu_4b_open_1_zero), .Less(Less), .Cin(Cin), .x(x[3:0]), .y(y[3:0]), .Op(Op));
  alu_4b_open alu_4b_open_2 (
    .O(alu_4b_open_2_o), .SET(alu_4b_open_2_set), .COUT(alu_4b_open_2_cout), .R(R[7:4]),
    .ZERO(alu_4b_open_2_zero), .Less(1'b0), .Cin(alu_4b_open_1_cout), .x(x[7:4]), .y(y[7:4]), .Op(Op));
  alu_4b_open alu_4b_open_3 (
    .O(alu_4b_open_3_o), .SET(alu_4b_open_3_set), .COUT(alu_4b_open_3_cout), .R(R[11:8]),
    .ZERO(alu_4b_open_3_zero), .Less(1'b0), .Cin(alu_4b_open_2_cout), .x(x[11:8]), .y(y[11:8]), .Op(Op));
  alu_4b_open alu_4b_open_4 (
    .O(O), .SET(SET), .COUT(COUT), .R(R[15:12]), .ZERO(alu_4b_open_4_zero), .Less(1'b0),
    .Cin(alu_4b_open_3_cout), .x(x[15:12]), .y(y[15:12]), .Op(Op));
  // NoConnect on alu_4b_open_1_o
  // NoConnect on alu_4b_open_1_set
  // NoConnect on alu_4b_open_2_o
  // NoConnect on alu_4b_open_2_set
  // NoConnect on alu_4b_open_3_o
  // NoConnect on alu_4b_open_3_set
  and and_1 (ZERO, alu_4b_open_1_zero, alu_4b_open_2_zero, alu_4b_open_3_zero, alu_4b_open_4_zero);
endmodule

// ALU 16B
module alu_16b (
  input  [2:0] Op,
  input  [15:0] x,
  input  [15:0] y,
  output [15:0] R,
  output O,
  output ZERO
);

  wire alu_16b_open_1_cout, alu_16b_open_1_set;

  alu_16b_open alu_16b_open_1 (
    .O(O), .SET(alu_16b_open_1_set), .COUT(alu_16b_open_1_cout), .R(R), .ZERO(ZERO),
    .Less(alu_16b_open_1_set), .Cin(Op[2]), .x(x), .y(y), .Op(Op));
  // NoConnect on alu_16b_open_1_cout
endmodule
